# Fritzing sketch cbr-wiring (saved by Fritzing 0.9.3b)

parts:
  C1-M = Molex Picoblade Series Header [part_number=0533980871 package=Picoblade-53398-0871]  # not connected
  C1-F = Molex Picoblade Series Header [part_number=0533980871 package=Picoblade-53398-0871]
  ECU-OBD = Molex Picoblade Series Header [part_number=0533980371 package=Picoblade-53398-0371]
  C3-F = Molex Picoblade Series Header [part_number=0533980871 package=Picoblade-53398-0871]
  BAT-FUSE = Molex Picoblade Series Header [part_number=0533980271 package=Picoblade-53398-0271]  # not connected

nets:
  N1: C1-F.1, ECU-OBD.1
  N2: C1-F.2, ECU-OBD.2
  N3: C1-F.3, ECU-OBD.3
  N4: C1-F.4, C3-F.2, C3-F.3, C3-F.4
  N5: C1-F.5, C3-F.5
  N6: C1-F.6, C3-F.6
  N7: C1-F.7, C3-F.7
  N8: C1-F.8, C3-F.8
